// Digital circuit ALU32BIt_updated.dig as structural Verilog
module ALU32BIt_updated (
  input  [31:0] A,
  input  [31:0] B,
  input  c_in,
  output [31:0] result,
  output c_out
);

  Add #(.Bits(32)) Adder (.a(A), .b(B), .c_i(c_in), .s(result), .c_o(c_out));
endmodule
