// Digital circuit ALU32Bit.dig as structural Verilog
module ALU32Bit (
  input  a_0,
  input  b_0,
  input  c_in,
  input  a_1,
  input  b_1,
  input  a_2,
  input  b_2,
  input  a_3,
  input  b_3,
  input  a_4,
  input  b_4,
  input  a_5,
  input  b_5,
  input  a_6,
  input  b_6,
  input  a_7,
  input  b_7,
  input  a_8,
  input  b_8,
  input  a_9,
  input  b_9,
  input  a_10,
  input  b_10,
  input  a_11,
  input  b_11,
  input  a_12,
  input  b_12,
  input  a_13,
  input  b_13,
  input  a_14,
  input  b_14,
  input  a_15,
  input  b_15,
  input  a_16,
  input  b_16,
  input  a_17,
  input  b_17,
  input  a_18,
  input  b_18,
  input  a_19,
  input  b_19,
  input  a_20,
  input  b_20,
  input  a_21,
  input  b_21,
  input  a_22,
  input  b_22,
  input  a_23,
  input  b_23,
  input  a_24,
  input  b_24,
  input  a_25,
  input  b_25,
  input  a_26,
  input  b_26,
  input  a_27,
  input  b_27,
  input  a_28,
  input  b_28,
  input  a_29,
  input  b_29,
  input  a_30,
  input  b_30,
  input  a_31,
  input  b_31,
  input  [1:0] in_98,
  output R_0,
  output R_1,
  output R_2,
  output R_3,
  output R_4,
  output R_5,
  output R_6,
  output R_7,
  output R_8,
  output R_9,
  output R_10,
  output R_11,
  output R_12,
  output R_13,
  output R_14,
  output R_15,
  output R_16,
  output R_17,
  output R_18,
  output R_19,
  output R_20,
  output R_21,
  output R_22,
  output R_23,
  output R_24,
  output R_25,
  output R_26,
  output R_27,
  output R_28,
  output R_29,
  output R_30,
  output R_31
);

  wire alu1bit_1_c_out, alu1bit_2_c_out, alu1bit_3_c_out, alu1bit_4_c_out, alu1bit_5_c_out, alu1bit_6_c_out,
       alu1bit_7_c_out, alu1bit_8_c_out, alu1bit_9_c_out, alu1bit_10_c_out, alu1bit_11_c_out,
       alu1bit_12_c_out, alu1bit_13_c_out, alu1bit_14_c_out, alu1bit_15_c_out, alu1bit_16_c_out,
       alu1bit_17_c_out, alu1bit_18_c_out, alu1bit_19_c_out, alu1bit_20_c_out, alu1bit_21_c_out,
       alu1bit_22_c_out, alu1bit_23_c_out, alu1bit_24_c_out, alu1bit_25_c_out, alu1bit_26_c_out,
       alu1bit_27_c_out, alu1bit_28_c_out, alu1bit_29_c_out, alu1bit_30_c_out, alu1bit_31_c_out,
       alu1bit_32_c_out;

  ALU1Bit alu1bit_1 (.a(a_0), .b(b_0), .oper(in_98), .c_in(c_in), .c_out(alu1bit_1_c_out), .res(R_0));
  ALU1Bit alu1bit_2 (.a(a_1), .b(b_1), .oper(in_98), .c_in(alu1bit_1_c_out), .c_out(alu1bit_2_c_out), .res(R_1));
  ALU1Bit alu1bit_3 (.a(a_2), .b(b_2), .oper(in_98), .c_in(alu1bit_2_c_out), .c_out(alu1bit_3_c_out), .res(R_2));
  ALU1Bit alu1bit_4 (.a(a_3), .b(b_3), .oper(in_98), .c_in(alu1bit_3_c_out), .c_out(alu1bit_4_c_out), .res(R_3));
  ALU1Bit alu1bit_5 (.a(a_4), .b(b_4), .oper(in_98), .c_in(alu1bit_4_c_out), .c_out(alu1bit_5_c_out), .res(R_4));
  ALU1Bit alu1bit_6 (.a(a_5), .b(b_5), .oper(in_98), .c_in(alu1bit_5_c_out), .c_out(alu1bit_6_c_out), .res(R_5));
  ALU1Bit alu1bit_7 (.a(a_6), .b(b_6), .oper(in_98), .c_in(alu1bit_6_c_out), .c_out(alu1bit_7_c_out), .res(R_6));
  ALU1Bit alu1bit_8 (.a(a_7), .b(b_7), .oper(in_98), .c_in(alu1bit_7_c_out), .c_out(alu1bit_8_c_out), .res(R_7));
  ALU1Bit alu1bit_9 (.a(a_8), .b(b_8), .oper(in_98), .c_in(alu1bit_8_c_out), .c_out(alu1bit_9_c_out), .res(R_8));
  ALU1Bit alu1bit_10 (.a(a_9), .b(b_9), .oper(in_98), .c_in(alu1bit_9_c_out), .c_out(alu1bit_10_c_out), .res(R_9));
  ALU1Bit alu1bit_11 (.a(a_10), .b(b_10), .oper(in_98), .c_in(alu1bit_10_c_out), .c_out(alu1bit_11_c_out), .res(R_10));
  ALU1Bit alu1bit_12 (.a(a_11), .b(b_11), .oper(in_98), .c_in(alu1bit_11_c_out), .c_out(alu1bit_12_c_out), .res(R_11));
  ALU1Bit alu1bit_13 (.a(a_12), .b(b_12), .oper(in_98), .c_in(alu1bit_12_c_out), .c_out(alu1bit_13_c_out), .res(R_12));
  ALU1Bit alu1bit_14 (.a(a_13), .b(b_13), .oper(in_98), .c_in(alu1bit_13_c_out), .c_out(alu1bit_14_c_out), .res(R_13));
  ALU1Bit alu1bit_15 (.a(a_14), .b(b_14), .oper(in_98), .c_in(alu1bit_14_c_out), .c_out(alu1bit_15_c_out), .res(R_14));
  ALU1Bit alu1bit_16 (.a(a_15), .b(b_15), .oper(in_98), .c_in(alu1bit_15_c_out), .c_out(alu1bit_16_c_out), .res(R_15));
  ALU1Bit alu1bit_17 (.a(a_16), .b(b_16), .oper(in_98), .c_in(alu1bit_16_c_out), .c_out(alu1bit_17_c_out), .res(R_16));
  ALU1Bit alu1bit_18 (.a(a_17), .b(b_17), .oper(in_98), .c_in(alu1bit_17_c_out), .c_out(alu1bit_18_c_out), .res(R_17));
  ALU1Bit alu1bit_19 (.a(a_18), .b(b_18), .oper(in_98), .c_in(alu1bit_18_c_out), .c_out(alu1bit_19_c_out), .res(R_18));
  ALU1Bit alu1bit_20 (.a(a_19), .b(b_19), .oper(in_98), .c_in(alu1bit_19_c_out), .c_out(alu1bit_20_c_out), .res(R_19));
  ALU1Bit alu1bit_21 (.a(a_20), .b(b_20), .oper(in_98), .c_in(alu1bit_20_c_out), .c_out(alu1bit_21_c_out), .res(R_20));
  ALU1Bit alu1bit_22 (.a(a_21), .b(b_21), .oper(in_98), .c_in(alu1bit_21_c_out), .c_out(alu1bit_22_c_out), .res(R_21));
  ALU1Bit alu1bit_23 (.a(a_22), .b(b_22), .oper(in_98), .c_in(alu1bit_22_c_out), .c_out(alu1bit_23_c_out), .res(R_22));
  ALU1Bit alu1bit_24 (.a(a_23), .b(b_23), .oper(in_98), .c_in(alu1bit_23_c_out), .c_out(alu1bit_24_c_out), .res(R_23));
  ALU1Bit alu1bit_25 (.a(a_24), .b(b_24), .oper(in_98), .c_in(alu1bit_24_c_out), .c_out(alu1bit_25_c_out), .res(R_24));
  ALU1Bit alu1bit_26 (.a(a_25), .b(b_25), .oper(in_98), .c_in(alu1bit_25_c_out), .c_out(alu1bit_26_c_out), .res(R_25));
  ALU1Bit alu1bit_27 (.a(a_26), .b(b_26), .oper(in_98), .c_in(alu1bit_26_c_out), .c_out(alu1bit_27_c_out), .res(R_26));
  ALU1Bit alu1bit_28 (.a(a_27), .b(b_27), .oper(in_98), .c_in(alu1bit_27_c_out), .c_out(alu1bit_28_c_out), .res(R_27));
  ALU1Bit alu1bit_29 (.a(a_28), .b(b_28), .oper(in_98), .c_in(alu1bit_28_c_out), .c_out(alu1bit_29_c_out), .res(R_28));
  ALU1Bit alu1bit_30 (.a(a_29), .b(b_29), .oper(in_98), .c_in(alu1bit_29_c_out), .c_out(alu1bit_30_c_out), .res(R_29));
  ALU1Bit alu1bit_31 (.a(a_30), .b(b_30), .oper(in_98), .c_in(alu1bit_30_c_out), .c_out(alu1bit_31_c_out), .res(R_30));
  ALU1Bit alu1bit_32 (.a(a_31), .b(b_31), .oper(in_98), .c_in(alu1bit_31_c_out), .c_out(alu1bit_32_c_out), .res(R_31));

  // Notes on the sheet:
  //   Operation
endmodule
