// Digital circuit ALUControl.dig as structural Verilog
module ALUControl (
  input  ALUOp0,
  input  ALUOp1,
  input  [3:0] F,
  output [3:0] Operation
);

  wire and_1_out, not_1_out, not_2_out, not_3_out, or_1_out;

  or or_1 (or_1_out, F[3], F[0]);
  and and_1 (and_1_out, ALUOp1, F[1]);
  and and_2 (Operation[0], ALUOp1, or_1_out);
  not not_1 (not_1_out, ALUOp0);
  not not_2 (not_2_out, ALUOp1);
  not not_3 (not_3_out, F[2]);
  and and_3 (Operation[3], ALUOp0, not_1_out);
  or or_2 (Operation[2], ALUOp0, and_1_out);
  or or_3 (Operation[1], not_2_out, not_3_out);
  // Pins of 1 and 4 bits meet at Operation
endmodule
