// Digital circuit ALU1Bit.dig as structural Verilog
module ALU1Bit (
  input  a,
  input  b,
  input  [1:0] oper,
  input  c_in,
  output c_out,
  output res
);

  wire and_1_out, notconnected_1_out, or_1_out;

  and and_1 (and_1_out, a, b);
  or or_1 (or_1_out, a, b);
  CarryOut carryout_1 (.a(a), .b(b), .c_in(c_in), .c_out(c_out));
  // NotConnected on notconnected_1_out
  Multiplexer #(.Selector_Bits(2)) multiplexer_1 (
    .sel(oper), .in_0(and_1_out), .in_1(or_1_out), .in_2(c_out), .in_3(notconnected_1_out), .out(res));
endmodule
