// Digital circuit alu_control_unit.dig as structural Verilog
module alu_control_unit (
  input  ALUin1,
  input  ALUin0,
  input  I30,
  input  I14,
  input  I13,
  input  I12,
  output ALUc2,
  output ALUc3,
  output ALUc1,
  output ALUc0
);

  wire and3bit_1_out, and_1_out, and_2_out, and_3_out, and_4_out, not_1_out, not_2_out, not_3_out, not_4_out,
       not_5_out, not_6_out, not_7_out, not_8_out, not_9_out;

  not not_1 (not_1_out, I12);
  not not_2 (not_2_out, ALUin0);
  not not_3 (not_3_out, I30);
  And6bit and6bit_1 (.a0(ALUin1), .a1(not_2_out), .a2(not_3_out), .a3(I14), .a4(I13), .a5(not_1_out), .out(ALUc0));
  not not_4 (not_4_out, ALUin0);
  and and_1 (and_1_out, ALUin1, not_4_out);
  not not_5 (not_5_out, I12);
  not not_6 (not_6_out, I13);
  not not_7 (not_7_out, I14);
  And3bit and3bit_1 (.a0(not_7_out), .a1(not_6_out), .a2(not_5_out), .out(and3bit_1_out));
  not not_8 (not_8_out, ALUin1);
  and and_2 (and_2_out, not_8_out, ALUin0);
  and and_3 (and_3_out, and3bit_1_out, and_1_out);
  not not_9 (not_9_out, ALUin1);
  and and_4 (and_4_out, I30, and_3_out);
  or or_1 (ALUc1, and_3_out, not_9_out);
  or or_2 (ALUc2, and_2_out, and_4_out);

  assign ALUc3 = 1'b0;
endmodule
