// Digital circuit InstructionMemory.dig as structural Verilog
module InstructionMemory (
  input  Clk,
  input  [23:0] Loc_addr,
  input  [31:0] Data_in,
  input  WriteToMem,
  output [31:0] Data_out
);

  BlockRAMDualPort #(.AddrBits(24), .Bits(32)) Memory (
    .A(Loc_addr), .Din(Data_in), .str(WriteToMem), .C(Clk), .D(Data_out));
endmodule
