// Digital circuit CPU.dig as structural Verilog
module CPU (
  input  Clock,
  output [31:0] PC_val,
  output [3:0] State_out,
  output [31:0] A_reg,
  output [31:0] B_reg,
  output [31:0] Imm,
  output [31:0] Al_out,
  output ALU_a,
  output [1:0] ALU_b,
  output [3:0] ALU_in,
  output [31:0] MemDataRegOut,
  output [31:0] op_1,
  output [31:0] op_2,
  output [31:0] I_out
);

  wire ALU_zero, ALUOp0, ALUOp1, branch_out, ControlUnit_iord, ControlUnit_pcsource0, ControlUnit_pcsource1,
       ControlUnit_pcwrite, IRWrite, JalControl, JalrControl, LuiControl, Mem_Read, Mem_Write, MemToReg,
       or_1_out, or_2_out, PC_write_branch, RegWrite;
  wire [3:0] ControlUnit_ns_3;
  wire [23:0] multiplexer_1_out, multiplexer_8_out;
  wire [31:0] ALU_alu_out, and_1_out, lui_out, Mem_Dummy_d, multiplexer_2_out, multiplexer_6_out,
       multiplexer_7_out, not_1_out, RegFile_value1, RegFile_value2, t_alu_out, t_jal_tmp;
  wire [31:24] multiplexer_8_out_2;

  Register #(.Bits(32)) PC (.D(multiplexer_7_out), .C(Clock), .en(or_1_out), .Q(PC_val));
  or or_1 (or_1_out, ControlUnit_pcwrite, branch_out);
  Multiplexer #(.Bits(24)) multiplexer_1 (
    .sel(ControlUnit_iord), .in_0(PC_val[25:2]), .in_1(multiplexer_8_out), .out(multiplexer_1_out));
  RAMDualPort #(.AddrBits(24), .isProgramMemory("true"), .Bits(32)) Mem_Dummy (
    .A(multiplexer_1_out), .Din(B_reg), .str(Mem_Write), .C(Clock), .ld(Mem_Read), .D(Mem_Dummy_d));
  Register #(.Bits(32)) Instr_Reg (.D(Mem_Dummy_d), .C(Clock), .en(IRWrite), .Q(I_out));
  Register #(.Bits(32)) MemDataReg (.D(Mem_Dummy_d), .C(Clock), .en(1'b1), .Q(MemDataRegOut));
  Register #(.Bits(4)) STATE_REG (.D(ControlUnit_ns_3), .C(Clock), .en(1'b1), .Q(State_out));
  OPCodeControlUnit ControlUnit (
    .I0(I_out[0]), .I1(I_out[1]), .I2(I_out[2]), .I3(I_out[3]), .I4(I_out[4]), .I5(I_out[5]), .I6(I_out[6]),
    .S_0(State_out[0]), .S_1(State_out[1]), .S_2(State_out[2]), .S_3(State_out[3]),
    .PCWrite(ControlUnit_pcwrite), .PCWriteCond(PC_write_branch), .IorD(ControlUnit_iord),
    .MemWrite(Mem_Write), .MemRead(Mem_Read), .IRWrite(IRWrite), .MemtoReg(MemToReg),
    .PCSource0(ControlUnit_pcsource0), .PCSource1(ControlUnit_pcsource1), .ALUOp0(ALUOp0), .ALUOp1(ALUOp1),
    .ALUSrcB1(ALU_b[1]), .ALUSrcB0(ALU_b[0]), .ALUSrcA(ALU_a), .RegWrite(RegWrite),
    .NS_0(ControlUnit_ns_3[0]), .NS_1(ControlUnit_ns_3[1]), .NS_2(ControlUnit_ns_3[2]),
    .NS_3(ControlUnit_ns_3[3]), .LuiSrc(LuiControl), .JalControl(JalControl), .JalrControl(JalrControl));
  Multiplexer #(.Bits(32)) multiplexer_2 (
    .sel(MemToReg), .in_0({multiplexer_8_out_2, multiplexer_8_out}), .in_1(MemDataRegOut),
    .out(multiplexer_2_out));
  ImmediateGenerator immediategenerator_1 (.Ins(I_out), .imm(Imm));
  RegFile32Bit RegFile (
    .DataToWrite(multiplexer_2_out), .writeEnable(RegWrite), .writeReg(I_out[11:7]), .Read1(I_out[19:15]),
    .Read2(I_out[24:20]), .CPU_clock(Clock), .value1(RegFile_value1), .value2(RegFile_value2));
  Register #(.Bits(32)) u_A_reg (.D(RegFile_value1), .C(Clock), .en(1'b1), .Q(A_reg));
  Register #(.Bits(32)) u_B_reg (.D(RegFile_value2), .C(Clock), .en(1'b1), .Q(B_reg));
  or or_2 (or_2_out, ControlUnit_pcsource0, ControlUnit_pcsource1);
  Multiplexer #(.Bits(32)) multiplexer_3 (.sel(ALU_a), .in_0(PC_val), .in_1(A_reg), .out(op_1));
  Multiplexer #(.Selector_Bits(2), .Bits(32)) multiplexer_4 (
    .sel(ALU_b), .in_0(B_reg), .in_1(32'h4), .in_2(Imm), .in_3({32{1'b0}}), .out(op_2));
  alu_control_unit_2 alu_control_unit_2_1 (
    .ALUop({ALUOp1, ALUOp0}), .F({I_out[30], I_out[14:12]}), .Itype(I_out[5]), .Operation(ALU_in));
  ALU32Bit ALU (.Operation(ALU_in), .a(op_1), .b(op_2), .ALU_out(ALU_alu_out), .zero(ALU_zero));  // open: c_out
  Multiplexer #(.Bits(32)) multiplexer_5 (.sel(LuiControl), .in_0(ALU_alu_out), .in_1(lui_out), .out(Al_out));
  Multiplexer #(.Bits(32)) multiplexer_6 (.sel(or_2_out), .in_0(Al_out), .in_1(t_alu_out), .out(multiplexer_6_out));
  Register #(.Bits(32)) ALU_out (.D(Al_out), .C(Clock), .en(1'b1), .Q(t_alu_out));
  Multiplexer #(.Bits(32)) multiplexer_7 (
    .sel(JalrControl), .in_0(multiplexer_6_out), .in_1(and_1_out), .out(multiplexer_7_out));
  Multiplexer #(.Bits(32)) multiplexer_8 (
    .sel(JalControl), .in_0(t_alu_out), .in_1(t_jal_tmp), .out({multiplexer_8_out_2, multiplexer_8_out}));
  assign and_1_out = multiplexer_6_out & not_1_out;  // And and_1, 32 bits wide
  assign not_1_out = ~32'h1;  // Not not_1, 32 bits wide
  branch_control_unit branch_control_unit_1 (
    .zr(ALU_zero), .ng(Al_out[31]), .Branch(PC_write_branch), .funct3(I_out[14:12]), .CBranch(branch_out));
  assign lui_out = I_out & 32'hfffff000;  // And and_2, 32 bits wide
  Register #(.Bits(32)) jal_tmp (.D(t_alu_out), .C(Clock), .en(1'b1), .Q(t_jal_tmp));

  // Other names for the same wires on the sheet: ALUSrcB[1:0] = ALU_b; ALUSrcA = ALU_a; inst[31:0] = I_out;
  //   I_Type = I_out[5]; Funct3[2:0] = I_out[14:12]; Bit_30 = I_out[30]
endmodule

/* Test case Arithmetic:
Clock PC_val State_out I_out op_1 op_2 ALU_in Al_out MemDataRegOut

program(0x93,0x2a40413,0x802523,0xfe0004e3)

let i = 0;
while (i < 200)
0 x x x x x x x x
1 x x x x x x x x
let i = i + 1;
end while
*/
