// Digital circuit ALU32Bit.dig as structural Verilog
module ALU32Bit (
  input  [3:0] Operation,
  input  [31:0] a,
  input  [31:0] b,
  output c_out,
  output [31:0] ALU_out,
  output zero
);

  wire alu1bit_1_c_out, alu1bit_1_zero, alu1bit_2_c_out, alu1bit_2_zero, alu1bit_3_c_out, alu1bit_3_zero,
       alu1bit_4_c_out, alu1bit_4_zero, alu1bit_5_c_out, alu1bit_5_zero, alu1bit_6_c_out, alu1bit_6_zero,
       alu1bit_7_c_out, alu1bit_7_zero, alu1bit_8_c_out, alu1bit_8_zero, alu1bit_9_c_out, alu1bit_9_zero,
       alu1bit_10_c_out, alu1bit_10_zero, alu1bit_11_c_out, alu1bit_11_zero, alu1bit_12_c_out,
       alu1bit_12_zero, alu1bit_13_c_out, alu1bit_14_c_out, alu1bit_14_zero, alu1bit_15_c_out,
       alu1bit_15_zero, alu1bit_16_c_out, alu1bit_16_zero, alu1bit_17_c_out, alu1bit_17_zero,
       alu1bit_18_c_out, alu1bit_18_zero, alu1bit_19_c_out, alu1bit_19_zero, alu1bit_20_c_out,
       alu1bit_20_zero, alu1bit_21_c_out, alu1bit_21_zero, alu1bit_22_c_out, alu1bit_22_zero,
       alu1bit_23_c_out, alu1bit_23_zero, alu1bit_24_c_out, alu1bit_24_zero, alu1bit_25_c_out,
       alu1bit_25_zero, alu1bit_26_c_out, alu1bit_26_zero, alu1bit_27_c_out, alu1bit_27_zero,
       alu1bit_28_c_out, alu1bit_28_zero, alu1bit_29_c_out, alu1bit_29_zero, alu1bit_30_c_out,
       alu1bit_30_zero, alu1bit_31_c_out, alu1bit_31_zero, alu1bit_32_zero;

  ALU1Bit alu1bit_1 (
    .a(a[0]), .b(b[0]), .Oper(Operation), .C_in(Operation[2]), .c_out(alu1bit_1_c_out), .res(ALU_out[0]),
    .zero(alu1bit_1_zero));
  ALU1Bit alu1bit_2 (
    .a(a[1]), .b(b[1]), .Oper(Operation), .C_in(alu1bit_1_c_out), .c_out(alu1bit_2_c_out), .res(ALU_out[1]),
    .zero(alu1bit_2_zero));
  ALU1Bit alu1bit_3 (
    .a(a[2]), .b(b[2]), .Oper(Operation), .C_in(alu1bit_2_c_out), .c_out(alu1bit_3_c_out), .res(ALU_out[2]),
    .zero(alu1bit_3_zero));
  ALU1Bit alu1bit_4 (
    .a(a[3]), .b(b[3]), .Oper(Operation), .C_in(alu1bit_3_c_out), .c_out(alu1bit_4_c_out), .res(ALU_out[3]),
    .zero(alu1bit_4_zero));
  ALU1Bit alu1bit_5 (
    .a(a[4]), .b(b[4]), .Oper(Operation), .C_in(alu1bit_4_c_out), .c_out(alu1bit_5_c_out), .res(ALU_out[4]),
    .zero(alu1bit_5_zero));
  ALU1Bit alu1bit_6 (
    .a(a[5]), .b(b[5]), .Oper(Operation), .C_in(alu1bit_5_c_out), .c_out(alu1bit_6_c_out), .res(ALU_out[5]),
    .zero(alu1bit_6_zero));
  ALU1Bit alu1bit_7 (
    .a(a[6]), .b(b[6]), .Oper(Operation), .C_in(alu1bit_6_c_out), .c_out(alu1bit_7_c_out), .res(ALU_out[6]),
    .zero(alu1bit_7_zero));
  ALU1Bit alu1bit_8 (
    .a(a[7]), .b(b[7]), .Oper(Operation), .C_in(alu1bit_7_c_out), .c_out(alu1bit_8_c_out), .res(ALU_out[7]),
    .zero(alu1bit_8_zero));
  ALU1Bit alu1bit_9 (
    .a(a[8]), .b(b[8]), .Oper(Operation), .C_in(alu1bit_8_c_out), .c_out(alu1bit_9_c_out), .res(ALU_out[8]),
    .zero(alu1bit_9_zero));
  ALU1Bit alu1bit_10 (
    .a(a[9]), .b(b[9]), .Oper(Operation), .C_in(alu1bit_9_c_out), .c_out(alu1bit_10_c_out), .res(ALU_out[9]),
    .zero(alu1bit_10_zero));
  ALU1Bit alu1bit_11 (
    .a(a[10]), .b(b[10]), .Oper(Operation), .C_in(alu1bit_10_c_out), .c_out(alu1bit_11_c_out),
    .res(ALU_out[10]), .zero(alu1bit_11_zero));
  ALU1Bit alu1bit_12 (
    .a(a[11]), .b(b[11]), .Oper(Operation), .C_in(alu1bit_11_c_out), .c_out(alu1bit_12_c_out),
    .res(ALU_out[11]), .zero(alu1bit_12_zero));
  ALU1Bit alu1bit_13 (
    .a(a[12]), .b(b[12]), .Oper(Operation), .C_in(alu1bit_12_c_out), .c_out(alu1bit_13_c_out),
    .res(ALU_out[12]));  // open: zero
  ALU1Bit alu1bit_14 (
    .a(a[13]), .b(b[13]), .Oper(Operation), .C_in(alu1bit_13_c_out), .c_out(alu1bit_14_c_out),
    .res(ALU_out[13]), .zero(alu1bit_14_zero));
  ALU1Bit alu1bit_15 (
    .a(a[14]), .b(b[14]), .Oper(Operation), .C_in(alu1bit_14_c_out), .c_out(alu1bit_15_c_out),
    .res(ALU_out[14]), .zero(alu1bit_15_zero));
  ALU1Bit alu1bit_16 (
    .a(a[15]), .b(b[15]), .Oper(Operation), .C_in(alu1bit_15_c_out), .c_out(alu1bit_16_c_out),
    .res(ALU_out[15]), .zero(alu1bit_16_zero));
  ALU1Bit alu1bit_17 (
    .a(a[16]), .b(b[16]), .Oper(Operation), .C_in(alu1bit_16_c_out), .c_out(alu1bit_17_c_out),
    .res(ALU_out[16]), .zero(alu1bit_17_zero));
  ALU1Bit alu1bit_18 (
    .a(a[17]), .b(b[17]), .Oper(Operation), .C_in(alu1bit_17_c_out), .c_out(alu1bit_18_c_out),
    .res(ALU_out[17]), .zero(alu1bit_18_zero));
  ALU1Bit alu1bit_19 (
    .a(a[18]), .b(b[18]), .Oper(Operation), .C_in(alu1bit_18_c_out), .c_out(alu1bit_19_c_out),
    .res(ALU_out[18]), .zero(alu1bit_19_zero));
  ALU1Bit alu1bit_20 (
    .a(a[19]), .b(b[19]), .Oper(Operation), .C_in(alu1bit_19_c_out), .c_out(alu1bit_20_c_out),
    .res(ALU_out[19]), .zero(alu1bit_20_zero));
  ALU1Bit alu1bit_21 (
    .a(a[20]), .b(b[20]), .Oper(Operation), .C_in(alu1bit_20_c_out), .c_out(alu1bit_21_c_out),
    .res(ALU_out[20]), .zero(alu1bit_21_zero));
  ALU1Bit alu1bit_22 (
    .a(a[21]), .b(b[21]), .Oper(Operation), .C_in(alu1bit_21_c_out), .c_out(alu1bit_22_c_out),
    .res(ALU_out[21]), .zero(alu1bit_22_zero));
  ALU1Bit alu1bit_23 (
    .a(a[22]), .b(b[22]), .Oper(Operation), .C_in(alu1bit_22_c_out), .c_out(alu1bit_23_c_out),
    .res(ALU_out[22]), .zero(alu1bit_23_zero));
  ALU1Bit alu1bit_24 (
    .a(a[23]), .b(b[23]), .Oper(Operation), .C_in(alu1bit_23_c_out), .c_out(alu1bit_24_c_out),
    .res(ALU_out[23]), .zero(alu1bit_24_zero));
  ALU1Bit alu1bit_25 (
    .a(a[24]), .b(b[24]), .Oper(Operation), .C_in(alu1bit_24_c_out), .c_out(alu1bit_25_c_out),
    .res(ALU_out[24]), .zero(alu1bit_25_zero));
  ALU1Bit alu1bit_26 (
    .a(a[25]), .b(b[25]), .Oper(Operation), .C_in(alu1bit_25_c_out), .c_out(alu1bit_26_c_out),
    .res(ALU_out[25]), .zero(alu1bit_26_zero));
  ALU1Bit alu1bit_27 (
    .a(a[26]), .b(b[26]), .Oper(Operation), .C_in(alu1bit_26_c_out), .c_out(alu1bit_27_c_out),
    .res(ALU_out[26]), .zero(alu1bit_27_zero));
  ALU1Bit alu1bit_28 (
    .a(a[27]), .b(b[27]), .Oper(Operation), .C_in(alu1bit_27_c_out), .c_out(alu1bit_28_c_out),
    .res(ALU_out[27]), .zero(alu1bit_28_zero));
  ALU1Bit alu1bit_29 (
    .a(a[28]), .b(b[28]), .Oper(Operation), .C_in(alu1bit_28_c_out), .c_out(alu1bit_29_c_out),
    .res(ALU_out[28]), .zero(alu1bit_29_zero));
  ALU1Bit alu1bit_30 (
    .a(a[29]), .b(b[29]), .Oper(Operation), .C_in(alu1bit_29_c_out), .c_out(alu1bit_30_c_out),
    .res(ALU_out[29]), .zero(alu1bit_30_zero));
  ALU1Bit alu1bit_31 (
    .a(a[30]), .b(b[30]), .Oper(Operation), .C_in(alu1bit_30_c_out), .c_out(alu1bit_31_c_out),
    .res(ALU_out[30]), .zero(alu1bit_31_zero));
  ALU1Bit alu1bit_32 (
    .a(a[31]), .b(b[31]), .Oper(Operation), .C_in(alu1bit_31_c_out), .c_out(c_out), .res(ALU_out[31]),
    .zero(alu1bit_32_zero));
  and and_1 (zero, alu1bit_1_zero, alu1bit_2_zero, alu1bit_3_zero, alu1bit_4_zero, alu1bit_5_zero, alu1bit_6_zero, alu1bit_7_zero, alu1bit_8_zero, alu1bit_9_zero, alu1bit_10_zero, alu1bit_11_zero, alu1bit_12_zero, alu1bit_14_zero, alu1bit_15_zero, alu1bit_16_zero, alu1bit_17_zero, alu1bit_18_zero, alu1bit_19_zero, alu1bit_19_c_out, alu1bit_20_zero, alu1bit_21_zero, alu1bit_22_zero, alu1bit_23_zero, alu1bit_24_zero, alu1bit_25_zero, alu1bit_26_zero, alu1bit_27_zero, alu1bit_28_zero, alu1bit_29_zero, alu1bit_30_zero, alu1bit_31_zero, alu1bit_32_zero);

  // Notes on the sheet:
  //   Operation: default 2
  //   a: default 6
  //   b: default 2
endmodule
