// Digital circuit OPCodeControlUnit.dig as structural Verilog
module OPCodeControlUnit (
  input  I0,
  input  I1,
  input  I2,
  input  I3,
  input  I4,
  input  I5,
  input  I6,
  input  S_0,
  input  S_1,
  input  S_2,
  input  S_3,
  output PCWrite,
  output PCWriteCond,
  output IorD,
  output MemWrite,
  output MemRead,
  output IRWrite,
  output MemtoReg,
  output PCSource0,
  output PCSource1,
  output ALUOp0,
  output ALUOp1,
  output ALUSrcB1,
  output ALUSrcB0,
  output ALUSrcA,
  output RegWrite,
  output NS_0,
  output NS_1,
  output NS_2,
  output NS_3,
  output LuiSrc,
  output JalControl,
  output JalrControl
);

  wire and_23_out, beq, I_Type, jal, jalr, lui, lw, NextState_2, NextState_3, NextState_4, NextState_5,
       NextState_6, NextState_7, NextState_8, NextState_9, NextState_10, NextState_11, NextState_12,
       NextState_13, NextState_14, nop, not_5_out, not_6_out, not_7_out, not_8_out, not_9_out, not_10_out,
       not_11_out, not_12_out, not_13_out, not_14_out, not_15_out, not_16_out, not_17_out, not_18_out,
       not_19_out, not_20_out, not_21_out, not_22_out, not_23_out, not_24_out, not_25_out, not_26_out,
       not_27_out, not_28_out, not_29_out, not_30_out, not_31_out, not_32_out, not_33_out, not_34_out,
       not_35_out, or_9_out, R_Type, S_0_D, S_1_D, S_2_D, S_3_D, State_1, State_2, State_6, State_7,
       State_10, State_12, State_14, sw;

  and and_1 (MemWrite, S_0, S_1_D, S_2, S_3_D);
  and and_2 (State_6, S_0_D, S_1, S_2, S_3_D);
  and and_3 (PCSource0, S_0_D, S_1_D, S_2_D, S_3_D);
  and and_4 (State_1, S_0, S_1_D, S_2_D, S_3_D);
  and and_5 (State_2, S_0_D, S_1, S_2_D, S_3_D);
  and and_6 (NextState_4, S_0, S_1, S_2_D, S_3_D);
  and and_7 (MemtoReg, S_0_D, S_1_D, S_2, S_3_D);
  and and_8 (State_7, S_0, S_1, S_2, S_3_D);
  and and_9 (ALUOp0, S_0_D, S_1_D, S_2_D, S_3);
  and and_10 (ALUSrcB0, S_0, S_1_D, S_2_D, S_3);
  and and_11 (State_10, S_0_D, S_1, S_2_D, S_3);
  and and_12 (LuiSrc, S_0, S_1, S_2_D, S_3);
  and and_13 (State_12, S_0_D, S_1_D, S_2, S_3);
  and and_14 (JalrControl, S_0, S_1_D, S_2, S_3);
  and and_15 (State_14, S_0_D, S_1, S_2, S_3);
  not not_1 (S_0_D, S_0);
  not not_2 (S_1_D, S_1);
  not not_3 (S_2_D, S_2);
  not not_4 (S_3_D, S_3);
  or or_1 (PCWrite, ALUSrcB0, State_12, PCSource0, JalrControl);
  or or_2 (IorD, NextState_4, MemWrite);
  or or_3 (MemRead, NextState_4, ALUSrcB0);
  or or_4 (ALUOp1, State_6, State_10);
  or or_5 (ALUSrcB1, State_1, State_12, JalrControl, State_2, State_10);
  or or_6 (ALUSrcA, State_2, State_6, ALUOp0, State_10, JalrControl);
  or or_7 (RegWrite, State_12, MemtoReg, JalrControl, State_7, PCSource0);
  or or_8 (JalControl, State_12, JalrControl);
  or or_9 (or_9_out, lw, sw);
  and and_16 (NextState_3, State_2, lw);
  and and_17 (NextState_6, State_1, R_Type);
  or or_10 (NextState_7, State_6, LuiSrc, State_10);
  and and_18 (NextState_8, State_1, beq);
  and and_19 (NextState_10, State_1, I_Type);
  and and_20 (NextState_11, State_1, lui);
  and and_21 (NextState_12, State_1, jal);
  and and_22 (NextState_13, State_1, jalr);
  and and_23 (and_23_out, State_1, nop);
  and and_24 (NextState_2, State_1, or_9_out);
  and and_25 (NextState_5, State_2, sw);
  or or_11 (NextState_9, State_12, MemtoReg, MemWrite, JalrControl, ALUOp0, PCSource0, State_7);
  or or_12 (NextState_14, and_23_out, State_14);
  or or_13 (NS_1, NextState_2, NextState_3, NextState_10, NextState_14, NextState_6, NextState_7, NextState_11);
  or or_14 (NS_2, NextState_4, NextState_5, NextState_12, NextState_14, NextState_6, NextState_13, NextState_7);
  or or_15 (NS_3, NextState_8, NextState_10, NextState_12, NextState_14, NextState_11, NextState_9, NextState_13);
  or or_16 (NS_0, ALUSrcB0, NextState_3, NextState_9, NextState_13, NextState_7, NextState_5, NextState_11);
  not not_5 (not_5_out, I6);
  not not_6 (not_6_out, I3);
  not not_7 (not_7_out, I2);
  And7Bit R_Front (.I0(I0), .I1(I1), .I2(not_7_out), .I3(not_6_out), .I4(I4), .I5(I5), .I6(not_5_out), .O(R_Type));
  not not_8 (not_8_out, I6);
  not not_9 (not_9_out, I5);
  not not_10 (not_10_out, I4);
  not not_11 (not_11_out, I3);
  not not_12 (not_12_out, I2);
  And7Bit u_lw (
    .I0(I0), .I1(I1), .I2(not_12_out), .I3(not_11_out), .I4(not_10_out), .I5(not_9_out), .I6(not_8_out),
    .O(lw));
  not not_13 (not_13_out, I6);
  not not_14 (not_14_out, I4);
  not not_15 (not_15_out, I3);
  not not_16 (not_16_out, I2);
  And7Bit u_sw (.I0(I0), .I1(I1), .I2(not_16_out), .I3(not_15_out), .I4(not_14_out), .I5(I5), .I6(not_13_out), .O(sw));
  not not_17 (not_17_out, I4);
  not not_18 (not_18_out, I3);
  not not_19 (not_19_out, I2);
  And7Bit u_beq (.I0(I0), .I1(I1), .I2(not_19_out), .I3(not_18_out), .I4(not_17_out), .I5(I5), .I6(I6), .O(beq));
  not not_20 (not_20_out, I6);
  not not_21 (not_21_out, I5);
  not not_22 (not_22_out, I3);
  not not_23 (not_23_out, I2);
  And7Bit I_Front (
    .I0(I0), .I1(I1), .I2(not_23_out), .I3(not_22_out), .I4(I4), .I5(not_21_out), .I6(not_20_out), .O(I_Type));
  not not_24 (not_24_out, I6);
  not not_25 (not_25_out, I3);
  And7Bit u_LUI (.I0(I0), .I1(I1), .I2(I2), .I3(not_25_out), .I4(I4), .I5(I5), .I6(not_24_out), .O(lui));
  not not_26 (not_26_out, I4);
  And7Bit u_JAL (.I0(I0), .I1(I1), .I2(I2), .I3(I3), .I4(not_26_out), .I5(I5), .I6(I6), .O(jal));
  not not_27 (not_27_out, I4);
  not not_28 (not_28_out, I3);
  And7Bit u_JALR (.I0(I0), .I1(I1), .I2(I2), .I3(not_28_out), .I4(not_27_out), .I5(I5), .I6(I6), .O(jalr));
  not not_29 (not_29_out, I6);
  not not_30 (not_30_out, I5);
  not not_31 (not_31_out, I4);
  not not_32 (not_32_out, I3);
  not not_33 (not_33_out, I2);
  not not_34 (not_34_out, I1);
  not not_35 (not_35_out, I0);
  And7Bit u_NOP (
    .I0(not_35_out), .I1(not_34_out), .I2(not_33_out), .I3(not_32_out), .I4(not_31_out), .I5(not_30_out),
    .I6(not_29_out), .O(nop));

  assign IRWrite = ALUSrcB0;
  assign PCSource1 = ALUOp0;
  assign PCWriteCond = ALUOp0;

  // Other names for the same wires on the sheet: State_0 = PCSource0; State_3 = NextState_4; State_4 = MemtoReg;
  //   State_5 = MemWrite; State_8 = ALUOp0; NextState_1 = ALUSrcB0; State_9 = ALUSrcB0; State_11 = LuiSrc;
  //   State_13 = JalrControl
endmodule
