// Digital circuit branch_control_unit.dig as structural Verilog
module branch_control_unit (
  input  zr,
  input  ng,
  input  Branch,
  input  [2:0] funct3,
  output CBranch
);

  wire BEQ_out, BGE_out, BGEU_out, BLT_out, BLTU_out, BNE_out, not_1_out, not_2_out, not_3_out, not_4_out,
       not_5_out, not_6_out, not_7_out, not_8_out, not_9_out, not_10_out, not_11_out, or6bit_1_out, or_1_out;

  not not_1 (not_1_out, ng);
  or or_1 (or_1_out, zr, not_1_out);
  not not_2 (not_2_out, funct3[2]);
  not not_3 (not_3_out, funct3[1]);
  not not_4 (not_4_out, funct3[0]);
  not not_5 (not_5_out, funct3[2]);
  not not_6 (not_6_out, funct3[1]);
  not not_7 (not_7_out, zr);
  not not_8 (not_8_out, funct3[1]);
  not not_9 (not_9_out, funct3[0]);
  not not_10 (not_10_out, funct3[1]);
  not not_11 (not_11_out, funct3[0]);
  And4bit BEQ (.a0(not_2_out), .a1(not_3_out), .a2(not_4_out), .a3(zr), .out(BEQ_out));
  And4bit BNE (.a0(not_5_out), .a1(not_6_out), .a2(funct3[0]), .a3(not_7_out), .out(BNE_out));
  And4bit BLT (.a0(funct3[2]), .a1(not_8_out), .a2(not_9_out), .a3(ng), .out(BLT_out));
  And4bit BGE (.a0(funct3[2]), .a1(not_10_out), .a2(funct3[0]), .a3(or_1_out), .out(BGE_out));
  And4bit BLTU (.a0(funct3[2]), .a1(funct3[1]), .a2(not_11_out), .a3(1'b0), .out(BLTU_out));
  And4bit BGEU (.a0(funct3[2]), .a1(funct3[1]), .a2(funct3[0]), .a3(1'b0), .out(BGEU_out));
  Or6bit or6bit_1 (
    .a0(BEQ_out), .a1(BNE_out), .a2(BLT_out), .a3(BGE_out), .a4(BLTU_out), .a5(BGEU_out), .out(or6bit_1_out));
  and and_1 (CBranch, or6bit_1_out, Branch);
endmodule
