// Digital circuit ImmGenB.dig as structural Verilog
module ImmGenB (
  input  [31:0] in,
  output [31:0] out
);

  BitExtender #(.inputBits(12), .outputBits(32)) bitextender_1 (.in({in[31], in[7], in[30:25], in[11:8]}), .out(out));
endmodule
