// Digital circuit ImmGenS.dig as structural Verilog
module ImmGenS (
  input  [31:0] in,
  output [31:0] out
);

  BitExtender #(.inputBits(12), .outputBits(32)) bitextender_1 (.in({in[31:25], in[11:7]}), .out(out));
endmodule
