// Digital circuit ImmediateGenerator.dig as structural Verilog
module ImmediateGenerator (
  input  [31:0] Ins,
  output [31:0] imm
);

  wire B_o, I1_o, I23_o, J_o, not_1_out, not_2_out, not_3_out, not_4_out, not_5_out, not_6_out, not_7_out,
       not_8_out, not_9_out, not_10_out, not_11_out, not_12_out, not_13_out, not_14_out, not_15_out,
       not_16_out, or_1_out, S_o, U_o;
  wire [2:0] opr_num;
  wire [31:0] immgenb_1_out, immgeni_1_out, immgenj_1_out, immgens_1_out, immgenu_1_out;

  ImmGenI immgeni_1 (.in(Ins), .out(immgeni_1_out));
  ImmGenS immgens_1 (.in(Ins), .out(immgens_1_out));
  ImmGenB immgenb_1 (.in(Ins), .out(immgenb_1_out));
  ImmGenJ immgenj_1 (.in(Ins), .out(immgenj_1_out));
  ImmGenU immgenu_1 (.in(Ins), .out(immgenu_1_out));
  not not_1 (not_1_out, Ins[6]);
  not not_2 (not_2_out, Ins[3]);
  And7Bit U (.I0(Ins[0]), .I1(Ins[1]), .I2(Ins[2]), .I3(not_2_out), .I4(Ins[4]), .I5(1'b1), .I6(not_1_out), .O(U_o));
  not not_3 (not_3_out, Ins[4]);
  And7Bit J (.I0(Ins[0]), .I1(Ins[1]), .I2(Ins[2]), .I3(Ins[3]), .I4(not_3_out), .I5(Ins[5]), .I6(Ins[6]), .O(J_o));
  not not_4 (not_4_out, Ins[4]);
  not not_5 (not_5_out, Ins[3]);
  not not_6 (not_6_out, Ins[2]);
  And7Bit B (
    .I0(Ins[0]), .I1(Ins[1]), .I2(not_6_out), .I3(not_5_out), .I4(not_4_out), .I5(Ins[5]), .I6(Ins[6]),
    .O(B_o));
  not not_7 (not_7_out, Ins[6]);
  not not_8 (not_8_out, Ins[4]);
  not not_9 (not_9_out, Ins[3]);
  PriorityEncoder #(.Selector_Bits(3)) opr (
    .in0(1'b1), .in1(1'b1), .in2(1'b1), .in3(or_1_out), .in4(S_o), .in5(B_o), .in6(J_o), .in7(U_o),
    .num(opr_num));  // open: any
  not not_10 (not_10_out, Ins[2]);
  And7Bit S (
    .I0(Ins[0]), .I1(Ins[1]), .I2(not_10_out), .I3(not_9_out), .I4(not_8_out), .I5(Ins[5]), .I6(not_7_out),
    .O(S_o));
  not not_11 (not_11_out, Ins[4]);
  not not_12 (not_12_out, Ins[3]);
  And7Bit I1 (
    .I0(Ins[0]), .I1(Ins[1]), .I2(Ins[2]), .I3(not_12_out), .I4(not_11_out), .I5(Ins[5]), .I6(Ins[6]),
    .O(I1_o));
  or or_1 (or_1_out, I23_o, I1_o);
  not not_13 (not_13_out, Ins[6]);
  not not_14 (not_14_out, Ins[5]);
  not not_15 (not_15_out, Ins[3]);
  Multiplexer #(.Selector_Bits(3), .Bits(32)) multiplexer_1 (
    .sel(opr_num), .in_0({32{1'b0}}), .in_1({32{1'b0}}), .in_2({32{1'b0}}), .in_3(immgeni_1_out),
    .in_4(immgens_1_out), .in_5(immgenb_1_out), .in_6(immgenj_1_out), .in_7(immgenu_1_out), .out(imm));
  not not_16 (not_16_out, Ins[2]);
  And7Bit I23 (
    .I0(Ins[0]), .I1(Ins[1]), .I2(not_16_out), .I3(not_15_out), .I4(1'b1), .I5(not_14_out), .I6(not_13_out),
    .O(I23_o));
endmodule
