// Digital circuit Or4bit.dig as structural Verilog
module Or4bit (
  input  a0,
  input  a1,
  input  a2,
  input  a3,
  output out
);

  wire or_1_out, or_2_out;

  or or_1 (or_1_out, a0, a1);
  or or_2 (or_2_out, a2, a3);
  or or_3 (out, or_1_out, or_2_out);
endmodule
