// Digital circuit alu_control_unit_2.dig as structural Verilog
module alu_control_unit_2 (
  input  [1:0] ALUop,
  input  [3:0] F,
  input  Itype,
  output [3:0] Operation
);

  wire _0000_out, _0X10_out, _0010_out, _1000_out, and_1_out, and_2_out, and_3_out, and_4_out, and_5_out,
       and_6_out, and_7_out, not_1_out, not_2_out, not_3_out, not_4_out, not_5_out, not_6_out, not_7_out,
       not_8_out, not_9_out, not_10_out, not_11_out, not_12_out, not_13_out, not_14_out, not_15_out,
       not_16_out;

  and and_1 (and_1_out, Itype, F[3]);
  not not_1 (not_1_out, ALUop[1]);
  not not_2 (not_2_out, and_1_out);
  not not_3 (not_3_out, F[2]);
  not not_4 (not_4_out, ALUop[0]);
  and and_2 (and_2_out, not_4_out, not_1_out);
  not not_5 (not_5_out, F[0]);
  And4bit _0010 (.a0(not_5_out), .a1(F[1]), .a2(not_3_out), .a3(not_2_out), .out(_0010_out));
  and and_3 (and_3_out, and_6_out, _0010_out);
  not not_6 (not_6_out, ALUop[1]);
  and and_4 (and_4_out, ALUop[0], not_6_out);
  not not_7 (not_7_out, F[2]);
  not not_8 (not_8_out, F[1]);
  not not_9 (not_9_out, F[0]);
  And4bit _1000 (.a0(not_9_out), .a1(not_8_out), .a2(not_7_out), .a3(and_1_out), .out(_1000_out));
  and and_5 (and_5_out, and_6_out, _1000_out);
  not not_10 (not_10_out, ALUop[0]);
  and and_6 (and_6_out, not_10_out, ALUop[1]);
  not not_11 (not_11_out, and_1_out);
  not not_12 (not_12_out, F[2]);
  not not_13 (not_13_out, F[1]);
  not not_14 (not_14_out, F[0]);
  And4bit _0000 (.a0(not_14_out), .a1(not_13_out), .a2(not_12_out), .a3(not_11_out), .out(_0000_out));
  and and_7 (and_7_out, and_6_out, _0000_out);
  not not_15 (not_15_out, and_1_out);
  not not_16 (not_16_out, F[0]);
  And4bit _0X10 (.a0(not_16_out), .a1(F[1]), .a2(1'b1), .a3(not_15_out), .out(_0X10_out));
  and and_8 (Operation[0], and_6_out, _0X10_out);
  Or4bit or4bit_1 (.a0(and_4_out), .a1(and_5_out), .a2(and_3_out), .a3(1'b0), .out(Operation[2]));
  Or6bit or6bit_1 (
    .a0(and_4_out), .a1(and_2_out), .a2(and_7_out), .a3(and_5_out), .a4(and_3_out), .a5(1'b0),
    .out(Operation[1]));

  assign Operation[3] = 1'b0;
endmodule
