// Digital circuit And3bit.dig as structural Verilog
module And3bit (
  input  a0,
  input  a1,
  input  a2,
  output out
);

  wire and_1_out;

  and and_1 (and_1_out, a0, a1);
  and and_2 (out, and_1_out, a2);
endmodule
