// Digital circuit And4bit.dig as structural Verilog
module And4bit (
  input  a0,
  input  a1,
  input  a2,
  input  a3,
  output out
);

  wire and_1_out, and_2_out;

  and and_1 (and_1_out, a0, a1);
  and and_2 (and_2_out, a2, a3);
  and and_3 (out, and_1_out, and_2_out);
endmodule
