// Digital circuit OPCodeControlUnit.dig as structural Verilog
module OPCodeControlUnit (
  input  I0,
  input  I1,
  input  I2,
  input  I3,
  input  I4,
  input  I5,
  input  I6,
  output ALU_src,
  output MemtoReg,
  output RegWrite,
  output MemRead,
  output MemWrite,
  output Branch,
  output ALUop1,
  output ALUop0
);

  wire not_1_out, not_2_out, not_3_out, not_4_out, not_5_out, not_6_out, not_7_out, not_8_out, not_9_out,
       not_10_out, not_11_out, not_12_out, not_13_out, not_14_out, not_15_out;

  not not_1 (not_1_out, I6);
  not not_2 (not_2_out, I3);
  not not_3 (not_3_out, I2);
  And7Bit R_Front (.I0(I0), .I1(I1), .I2(not_3_out), .I3(not_2_out), .I4(I4), .I5(I5), .I6(not_1_out), .O(ALUop1));
  not not_4 (not_4_out, I6);
  not not_5 (not_5_out, I5);
  not not_6 (not_6_out, I4);
  not not_7 (not_7_out, I3);
  not not_8 (not_8_out, I2);
  And7Bit lw (
    .I0(I0), .I1(I1), .I2(not_8_out), .I3(not_7_out), .I4(not_6_out), .I5(not_5_out), .I6(not_4_out),
    .O(MemRead));
  not not_9 (not_9_out, I6);
  not not_10 (not_10_out, I4);
  not not_11 (not_11_out, I3);
  not not_12 (not_12_out, I2);
  And7Bit sw (
    .I0(I0), .I1(I1), .I2(not_12_out), .I3(not_11_out), .I4(not_10_out), .I5(I5), .I6(not_9_out), .O(MemWrite));
  not not_13 (not_13_out, I4);
  not not_14 (not_14_out, I3);
  not not_15 (not_15_out, I2);
  And7Bit beq (.I0(I0), .I1(I1), .I2(not_15_out), .I3(not_14_out), .I4(not_13_out), .I5(I5), .I6(I6), .O(ALUop0));
  or or_1 (ALU_src, MemRead, MemWrite);
  or or_2 (RegWrite, ALUop1, MemRead);

  assign Branch = ALUop0;
  assign MemtoReg = MemRead;
endmodule
