// Digital circuit And6bit.dig as structural Verilog
module And6bit (
  input  a0,
  input  a1,
  input  a2,
  input  a3,
  input  a4,
  input  a5,
  output out
);

  wire and3bit_1_out, and3bit_2_out;

  And3bit and3bit_1 (.a0(a0), .a1(a1), .a2(a2), .out(and3bit_1_out));
  And3bit and3bit_2 (.a0(a3), .a1(a4), .a2(a5), .out(and3bit_2_out));
  and and_1 (out, and3bit_1_out, and3bit_2_out);
endmodule
