// Digital circuit And7Bit.dig as structural Verilog
module And7Bit (
  input  I0,
  input  I1,
  input  I2,
  input  I3,
  input  I4,
  input  I5,
  input  I6,
  output O
);

  wire and_1_out, and_2_out, and_3_out, and_4_out, and_5_out, and_6_out;

  and and_1 (and_1_out, I0, I1);
  and and_2 (and_2_out, I2, I3);
  and and_3 (and_3_out, I4, I5);
  and and_4 (and_4_out, I6, 1'b1);
  and and_5 (and_5_out, and_1_out, and_2_out);
  and and_6 (and_6_out, and_3_out, and_4_out);
  and and_7 (O, and_5_out, and_6_out);
endmodule
