// Digital circuit Or6bit.dig as structural Verilog
module Or6bit (
  input  a0,
  input  a1,
  input  a2,
  input  a3,
  input  a4,
  input  a5,
  output out
);

  wire or_1_out, or_2_out, or_3_out, or_4_out;

  or or_1 (or_1_out, a0, a1);
  or or_2 (or_2_out, a2, a3);
  or or_3 (or_3_out, a4, a5);
  or or_4 (or_4_out, or_1_out, or_2_out);
  or or_5 (out, or_4_out, or_3_out);
endmodule
