// Digital circuit CPU.dig as structural Verilog
module CPU (
  input  Clock,
  output MemRead
);

  wire alu32bit_1_zero, branch_control_unit_1_cbranch, opcodecontrolunit_1_alu_src,
       opcodecontrolunit_1_aluop1, opcodecontrolunit_1_aluop2, opcodecontrolunit_1_branch,
       opcodecontrolunit_1_memtoreg, opcodecontrolunit_1_memwrite, opcodecontrolunit_1_regwrite;
  wire [3:0] alu_control_unit_1_operation;
  wire [6:0] instructionmemory_1_data_out;
  wire [31:0] adder32bit_1_sum, adder32bit_2_sum, alu32bit_1_alu_out, immediategenerator_1_imm,
       instructionmemory_2_data_out, multiplexer_1_out, multiplexer_2_out, multiplexer_3_out, PC_q,
       regfile32bit_1_value1, regfile32bit_1_value2;
  wire [31:7] instructionmemory_1_data_out_2;

  Register #(.Bits(32)) PC (.D(multiplexer_2_out), .C(Clock), .en(1'b1), .Q(PC_q));
  Adder32Bit adder32bit_1 (.B(PC_q), .A(32'h4), .C_in(1'b0), .sum(adder32bit_1_sum));  // open: c_out
  InstructionMemory instructionmemory_1 (
    .Clk(Clock), .Loc_addr(PC_q[23:0]), .Data_in({32{1'b0}}), .WriteToMem(1'b0),
    .Data_out({instructionmemory_1_data_out_2, instructionmemory_1_data_out}));
  OPCodeControlUnit opcodecontrolunit_1 (
    .I0(instructionmemory_1_data_out[6]), .I1(instructionmemory_1_data_out[5]),
    .I2(instructionmemory_1_data_out[4]), .I3(instructionmemory_1_data_out[3]),
    .I4(instructionmemory_1_data_out[2]), .I5(instructionmemory_1_data_out[1]),
    .I6(instructionmemory_1_data_out[0]), .ALU_src(opcodecontrolunit_1_alu_src),
    .MemtoReg(opcodecontrolunit_1_memtoreg), .RegWrite(opcodecontrolunit_1_regwrite), .MemRead(MemRead),
    .MemWrite(opcodecontrolunit_1_memwrite), .Branch(opcodecontrolunit_1_branch),
    .ALUop1(opcodecontrolunit_1_aluop1), .ALUop2(opcodecontrolunit_1_aluop2));
  RegFile32Bit regfile32bit_1 (
    .DataToWrite(multiplexer_3_out), .writeEnable(opcodecontrolunit_1_regwrite),
    .writeReg(instructionmemory_1_data_out_2[11:7]), .Read1(instructionmemory_1_data_out_2[19:15]),
    .Read2(instructionmemory_1_data_out_2[24:20]), .CPU_clock(Clock), .value1(regfile32bit_1_value1),
    .value2(regfile32bit_1_value2));
  ImmediateGenerator immediategenerator_1 (
    .Ins({instructionmemory_1_data_out_2, instructionmemory_1_data_out}), .imm(immediategenerator_1_imm));
  Multiplexer #(.Bits(32)) multiplexer_1 (
    .sel(opcodecontrolunit_1_alu_src), .in_0(regfile32bit_1_value2), .in_1(immediategenerator_1_imm),
    .out(multiplexer_1_out));
  ALU32Bit alu32bit_1 (
    .Operation(alu_control_unit_1_operation), .a(regfile32bit_1_value1), .b(multiplexer_1_out),
    .ALU_out(alu32bit_1_alu_out), .zero(alu32bit_1_zero));  // open: c_out
  alu_control_unit alu_control_unit_1 (
    .ALUin1(opcodecontrolunit_1_aluop2), .ALUin0(opcodecontrolunit_1_aluop1),
    .F({instructionmemory_1_data_out_2[14:12], instructionmemory_1_data_out_2[30]}),
    .Operation(alu_control_unit_1_operation));
  Adder32Bit adder32bit_2 (.B(immediategenerator_1_imm), .A(PC_q), .C_in(1'b0), .sum(adder32bit_2_sum));  // open: c_out
  Multiplexer #(.Bits(32)) multiplexer_2 (
    .sel(branch_control_unit_1_cbranch), .in_0(adder32bit_1_sum), .in_1(adder32bit_2_sum),
    .out(multiplexer_2_out));
  InstructionMemory instructionmemory_2 (
    .Clk(Clock), .Loc_addr(alu32bit_1_alu_out[23:0]), .Data_in(regfile32bit_1_value2),
    .WriteToMem(opcodecontrolunit_1_memwrite), .Data_out(instructionmemory_2_data_out));
  Multiplexer #(.Bits(32)) multiplexer_3 (
    .sel(opcodecontrolunit_1_memtoreg), .in_0(alu32bit_1_alu_out), .in_1(instructionmemory_2_data_out),
    .out(multiplexer_3_out));
  branch_control_unit branch_control_unit_1 (
    .zr(alu32bit_1_zero), .ng(alu32bit_1_alu_out[31]), .Branch(opcodecontrolunit_1_branch),
    .funct3(instructionmemory_1_data_out_2[14:12]), .CBranch(branch_control_unit_1_cbranch));
endmodule
