// Digital circuit ALU1Bit.dig as structural Verilog
module ALU1Bit (
  input  a,
  input  b,
  input  [3:0] Oper,
  input  C_in,
  output c_out,
  output res,
  output zero
);

  wire add_1_s, and_1_out, or_1_out, xor_1_out;

  xor xor_1 (xor_1_out, b, Oper[2]);
  and and_1 (and_1_out, a, xor_1_out);
  or or_1 (or_1_out, a, xor_1_out);
  Add add_1 (.a(a), .b(xor_1_out), .c_i(C_in), .s(add_1_s), .c_o(c_out));
  Multiplexer #(.Selector_Bits(3)) multiplexer_1 (
    .sel({Oper[3], Oper[1:0]}), .in_0(and_1_out), .in_1(or_1_out), .in_2(add_1_s), .in_3(1'b0), .in_4(1'b0),
    .in_5(1'b0), .in_6(1'b0), .in_7(1'b0), .out(res));
  not not_1 (zero, res);
endmodule
