// Digital circuit Adder32Bit.dig as structural Verilog
module Adder32Bit (
  input  [31:0] B,
  input  [31:0] A,
  input  C_in,
  output [31:0] sum,
  output c_out
);

  Add #(.Bits(32)) Adder (.a(A), .b(B), .c_i(C_in), .s(sum), .c_o(c_out));
endmodule
