// Digital circuit CarryOut.dig as structural Verilog
module CarryOut (
  input  a,
  input  b,
  input  c_in,
  output c_out
);

  wire and_1_out, and_2_out, and_3_out;

  and and_1 (and_1_out, c_in, a);
  and and_2 (and_2_out, c_in, b);
  and and_3 (and_3_out, a, b);
  or or_1 (c_out, and_1_out, and_2_out, and_3_out);
endmodule
