// Digital circuit ImmGenB.dig as structural Verilog
module ImmGenB (
  input  [31:0] in,
  output [31:0] out
);

  BitExtender #(.inputBits(13), .outputBits(32)) bitextender_1 (
    .in({in[31], in[7], in[30:25], in[11:8], 1'b0}), .out(out));
endmodule
