// Digital circuit ImmGenI.dig as structural Verilog
module ImmGenI (
  input  [31:0] in,
  output [31:0] out
);

  BitExtender #(.inputBits(12), .outputBits(32)) bitextender_1 (.in(in[31:20]), .out(out));
endmodule
