// Digital circuit ImmGenJ.dig as structural Verilog
module ImmGenJ (
  input  [31:0] in,
  output [31:0] out
);

  BitExtender #(.inputBits(21), .outputBits(32)) bitextender_1 (
    .in({in[31], in[19:12], in[20], in[30:21], 1'b0}), .out(out));
endmodule
