// Digital circuit RegFile32Bit.dig as structural Verilog
module RegFile32Bit (
  input  [31:0] DataToWrite,
  input  writeEnable,
  input  [4:0] writeReg,
  input  [4:0] Read1,
  input  [4:0] Read2,
  input  CPU_clock,
  output [31:0] Register1,
  output [31:0] Register2
);

  RegisterFile #(.AddrBits(5), .Bits(32)) RegFile (
    .Din(DataToWrite), .we(writeEnable), .Rw(writeReg), .C(CPU_clock), .Ra(Read1), .Rb(Read2),
    .Da(Register1), .Db(Register2));
endmodule
